# Fritzing sketch Esquema (saved by Fritzing 0.9.3b)
breadboards: 1

parts:
  Arduino_NANO_33_BLE = Arduino Nano (Rev3.0)
  Servo_MG995 = Dagu DGServo 9g (Top view) [part_number=RS001B]
  Alimentación = 4 x AAA Battery Mount

nets:
  N1: Arduino_NANO_33_BLE.D3, Servo_MG995.pulse
  N2: Servo_MG995.gnd, Alimentación.-
  N3: Servo_MG995.vcc, Alimentación.+
